# Fritzing sketch Ceng318Design (saved by Fritzing 0.9.3b)
circuit board: 9.31496cm x 5.38627cm
breadboards: 1

parts:
  STM32Duino_Blue_Pill = BluePill
  Willwin_MQ-2 = MQ-4

nets:
  N1: STM32Duino_Blue_Pill.A1, Willwin_MQ-2.AO
  3V3: STM32Duino_Blue_Pill.3V3, Willwin_MQ-2.VCC
  GND: STM32Duino_Blue_Pill.GND, Willwin_MQ-2.GND
  N2: STM32Duino_Blue_Pill.B8, Willwin_MQ-2.DO

notes:
  Smart Home Monitor
  Lucas Finiello
